// Logisim project Processador.circ as structural Verilog: 4 circuits, main circuit 74174
module main (
  input  _13_CLK,
  input  _2_M,
  input  _3_Cin,
  input  _4_S3,
  input  _5_S2,
  input  _6_S1,
  input  _7_S0,
  input  _8_MR,
  input  Write_Enable,
  input  A1_WR1,
  input  A0_WR0,
  input  _9_RA1_Im3,
  input  _10_RA0_Im2,
  input  _11_RB1_Im1,
  input  _12_RB0_Im0,
  output R0_3,
  output R0_2,
  output R0_1,
  output R0_0,
  output R1_3,
  output R1_2,
  output R1_1,
  output R1_0,
  output R2_3,
  output R2_2,
  output R2_1,
  output R2_0,
  output R3_3,
  output R3_2,
  output R3_1,
  output R3_1_2,
  output Y0,
  output Y1,
  output Y2,
  output Y3,
  output Cout,
  output A_B
);

  wire decoder_1_out0, decoder_1_out1, decoder_1_out2, decoder_1_out3, n7432_1_y0, n7432_1_y1, n7432_1_y2,
       n7432_1_y3, n7432_2_y0, n7432_2_y1, n7432_2_y2, n7432_2_y3, n74157_1_y0, n74157_1_y1, n74157_1_y2,
       n74157_1_y3, n74157_2_y0, n74157_2_y1, n74157_2_y2, n74157_2_y3, n74157_3_y0, n74157_3_y1,
       n74157_3_y2, n74157_3_y3, n74157_4_y0, n74157_4_y1, n74157_4_y2, n74157_4_y3, n74157_5_y0,
       n74157_5_y1, n74157_5_y2, n74157_5_y3, n74157_6_y0, n74157_6_y1, n74157_6_y2, n74181_1_p1,
       n74181_1_p10, n74181_1_p11, n74181_1_p12, not_1_out, not_2_out, not_3_out, not_4_out, not_5_out,
       R0_out, R1_out, R2_out, R3_out;

  Decoder #(.select(2)) decoder_1 (
    .out0(decoder_1_out0), .out1(decoder_1_out1), .out2(decoder_1_out2), .out3(decoder_1_out3),
    .sel({A1_WR1, A0_WR0}), .en(Write_Enable));
  not not_1 (not_1_out, decoder_1_out0);
  not not_2 (not_2_out, decoder_1_out1);
  not not_3 (not_3_out, decoder_1_out2);
  not not_4 (not_4_out, decoder_1_out3);
  or R0 (R0_out, _13_CLK, not_1_out);
  or R1 (R1_out, _13_CLK, not_2_out);
  or R2 (R2_out, _13_CLK, not_3_out);
  or R3 (R3_out, _13_CLK, not_4_out);
  _74157 u_74157_1 (
    .Y2(n74157_1_y2), .B2(R1_2), .A2(R0_2), .Y3(n74157_1_y3), .B3(R1_3), .A3(R0_3), .E_prime(1'b0),
    .Y1(n74157_1_y1), .B1(R1_1), .A1(R0_1), .Y0(n74157_1_y0), .B0(R1_0), .A0(R0_0), .S(n7432_2_y2));
  _74174 u_74174_1 (
    .D0(Y0), .Q0(R0_0), .D1(Y1), .Q1(R0_1), .CLK(R0_out), .CLR(1'b1), .D2(Y2), .Q2(R0_2), .D3(Y3), .Q3(R0_3));
  _74157 u_74157_2 (
    .Y2(n74157_2_y2), .B2(R3_2), .A2(R2_2), .Y3(n74157_2_y3), .B3(R3_3), .A3(R2_3), .E_prime(1'b0),
    .Y1(n74157_2_y1), .B1(R3_1), .A1(R2_1), .Y0(n74157_2_y0), .B0(R3_1_2), .A0(R2_0), .S(n7432_2_y2));
  _74174 u_74174_2 (
    .D0(Y0), .Q0(R1_0), .D1(Y1), .Q1(R1_1), .CLK(R1_out), .CLR(1'b1), .D2(Y2), .Q2(R1_2), .D3(Y3), .Q3(R1_3));
  _74157 u_74157_3 (
    .Y2(n74157_3_y2), .B2(n74157_2_y2), .A2(n74157_1_y2), .Y3(n74157_3_y3), .B3(n74157_2_y3),
    .A3(n74157_1_y3), .E_prime(1'b0), .Y1(n74157_3_y1), .B1(n74157_2_y1), .A1(n74157_1_y1), .Y0(n74157_3_y0),
    .B0(n74157_2_y0), .A0(n74157_1_y0), .S(n7432_2_y3));
  _74174 u_74174_3 (
    .D0(Y0), .Q0(R2_0), .D1(Y1), .Q1(R2_1), .CLK(R2_out), .CLR(1'b1), .D2(Y2), .Q2(R2_2), .D3(Y3), .Q3(R2_3));
  _74157 u_74157_4 (
    .Y2(n74157_4_y2), .B2(R1_2), .A2(R0_2), .Y3(n74157_4_y3), .B3(R1_3), .A3(R0_3), .E_prime(1'b0),
    .Y1(n74157_4_y1), .B1(R1_1), .A1(R0_1), .Y0(n74157_4_y0), .B0(R1_0), .A0(R0_0), .S(n7432_2_y0));
  _74157 u_74157_5 (
    .Y2(n74157_5_y2), .B2(R3_2), .A2(R2_2), .Y3(n74157_5_y3), .B3(R3_3), .A3(R2_3), .E_prime(1'b0),
    .Y1(n74157_5_y1), .B1(R3_1), .A1(R2_1), .Y0(n74157_5_y0), .B0(R3_1_2), .A0(R2_0), .S(n7432_2_y0));
  _74174 u_74174_4 (
    .D0(Y0), .Q0(R3_1_2), .D1(Y1), .Q1(R3_1), .CLK(R3_out), .CLR(1'b1), .D2(Y2), .Q2(R3_2), .D3(Y3), .Q3(R3_3));
  _74157 u_74157_6 (
    .Y2(n74157_6_y2), .B2(n74157_5_y2), .A2(n74157_4_y2), .Y3(n74157_5_y3), .B3(n74157_5_y3),
    .A3(n74157_4_y3), .E_prime(1'b0), .Y1(n74157_6_y1), .B1(n74157_5_y1), .A1(n74157_4_y1), .Y0(n74157_6_y0),
    .B0(n74157_5_y0), .A0(n74157_4_y0), .S(n7432_2_y1));
  _74157 u_74157_7 (
    .Y2(Y2), .B2(n7432_1_y2), .A2(n74181_1_p10), .Y3(Y3), .B3(n7432_1_y3), .A3(n74181_1_p1), .E_prime(1'b0),
    .Y1(Y1), .B1(n7432_1_y1), .A1(n74181_1_p11), .Y0(Y0), .B0(n7432_1_y0), .A0(n74181_1_p12), .S(_8_MR));
  // _74181 74181_1: pin names not known; wires that end beside it: n74181_1_p1, A_B, Cout, n74157_5_y3, n74157_3_y3, n74157_6_y2, n74157_3_y2, n74157_6_y1, n74157_3_y1, n74181_1_p10, n74181_1_p11, n74181_1_p12, _2_M, _3_Cin, _7_S0, _6_S1, _5_S2, _4_S3, n74157_3_y0, n74157_6_y0
  _7432 u_7432_1 (
    .Y2(n7432_1_y2), .B2(not_5_out), .A2(_10_RA0_Im2), .Y3(n7432_1_y3), .B3(not_5_out), .A3(_9_RA1_Im3),
    .Y1(n7432_1_y1), .B1(not_5_out), .A1(_11_RB1_Im1), .Y0(n7432_1_y0), .B0(not_5_out), .A0(_12_RB0_Im0));
  _7432 u_7432_2 (
    .Y2(n7432_2_y2), .B2(_8_MR), .A2(_10_RA0_Im2), .Y3(n7432_2_y3), .B3(_8_MR), .A3(_9_RA1_Im3),
    .Y1(n7432_2_y1), .B1(_8_MR), .A1(_11_RB1_Im1), .Y0(n7432_2_y0), .B0(_8_MR), .A0(_12_RB0_Im0));
  not not_5 (not_5_out, _8_MR);
endmodule

module _74157 (
  input  B2,
  input  B1,
  input  A2,
  input  A1,
  input  B3,
  input  B0,
  input  A3,
  input  A0,
  input  S,
  input  E_prime,
  output Y2,
  output Y1,
  output Y3,
  output Y0
);

  wire not_1_out;

  not not_1 (not_1_out, E_prime);
  Multiplexer multiplexer_1 (.in0(A1), .in1(B1), .out(Y1), .sel(S), .en(not_1_out));
  Multiplexer multiplexer_2 (.in0(A2), .in1(B2), .out(Y2), .sel(S), .en(not_1_out));
  Multiplexer multiplexer_3 (.in0(A3), .in1(B3), .out(Y3), .sel(S), .en(not_1_out));
  Multiplexer multiplexer_4 (.in0(A0), .in1(B0), .out(Y0), .sel(S), .en(not_1_out));
endmodule

module _7432 (
  input  B2,
  input  B1,
  input  A2,
  input  A1,
  input  B3,
  input  B0,
  input  A3,
  input  A0,
  output Y2,
  output Y1,
  output Y3,
  output Y0
);

  or or_1 (Y2, B2, A2);
  or or_2 (Y1, B1, A1);
  or or_3 (Y3, B3, A3);
  or or_4 (Y0, B0, A0);
endmodule

module _74174 (
  input  D0,
  input  D1,
  input  CLK,
  input  CLR,
  input  D2,
  input  D3,
  output Q0,
  output Q1,
  output Q2,
  output Q3
);

  D_Flip_Flop d_ff_1 (.clk(CLK), .D(D0), .Q(Q0), .en(CLR));  // open: Qn, preset, reset
  D_Flip_Flop d_ff_2 (.clk(CLK), .D(D2), .Q(Q2), .en(CLR));  // open: Qn, preset, reset
  D_Flip_Flop d_ff_3 (.clk(CLK), .D(D1), .Q(Q1), .en(CLR));  // open: Qn, preset, reset
  D_Flip_Flop d_ff_4 (.clk(CLK), .D(D3), .Q(Q3), .en(CLR));  // open: Qn, preset, reset
endmodule
